// Logisim project logisim_proj.circ as structural Verilog
module main (
);

  Counter #(.width(4), .max('hf)) counter_1 ();  // open: load, D, count, Q, carry, clk, clr
  Register #(.width(4)) register_1 ();  // open: D, en, Q, clk, clr
  ALU___74181 alu_74181_1 ();  // open: in_2, in_3, Y, C_n_4_prime, X, out_9, A_B, in_1, M, Cn_prime
  Register #(.width(4)) register_2 ();  // open: D, en, Q, clk, clr
  Register #(.width(4)) register_3 ();  // open: D, en, Q, clk, clr
  Register #(.width(4)) register_4 ();  // open: D, en, Q, clk, clr
  Register #(.width(4)) register_5 ();  // open: D, en, Q, clk, clr
  Register #(.width(4)) register_6 ();  // open: D, en, Q, clk, clr
  Register #(.width(4)) register_7 ();  // open: D, en, Q, clk, clr
  Control_Unit control_unit_1 ();
  RAM #(.dataWidth(4)) ram_1 ();  // open: addr, data, sel, clk, ld, clr
endmodule

module ALU___74181 (
  input  [3:0] in_1,
  input  [3:0] in_2,
  input  [3:0] in_3,
  input  M,
  input  Cn_prime,
  output Y,
  output C_n_4_prime,
  output X,
  output [3:0] out_9,
  output A_B
);

  wire and_1_out, and_2_out, and_3_out, and_4_out, and_5_out, and_6_out, and_7_out, and_8_out, and_9_out,
       and_10_out, and_11_out, and_12_out, and_13_out, and_14_out, and_15_out, and_16_out, and_17_out,
       and_18_out, and_19_out, and_20_out, and_21_out, and_22_out, and_23_out, and_24_out, and_25_out,
       and_26_out, and_27_out, and_28_out, nand_1_out, nand_3_out, nor_1_out, nor_2_out, nor_3_out,
       nor_4_out, nor_5_out, nor_6_out, nor_7_out, nor_8_out, nor_10_out, nor_11_out, nor_12_out, not_1_out,
       not_2_out, not_3_out, not_4_out, not_5_out, not_6_out, not_7_out, xor_1_out, xor_2_out, xor_3_out,
       xor_4_out;

  not not_1 (not_1_out, in_2[3]);
  not not_2 (not_2_out, in_2[2]);
  not not_3 (not_3_out, in_2[1]);
  not not_4 (not_4_out, in_2[0]);
  and and_1 (and_1_out, in_2[3], in_1[3], in_2[3]);
  and and_2 (and_2_out, in_2[3], in_1[2], not_1_out);
  and and_3 (and_3_out, not_1_out, in_1[1]);
  and and_4 (and_4_out, in_2[3], in_1[0]);
  and and_5 (and_5_out, in_2[2], in_1[3], in_2[2]);
  and and_6 (and_6_out, in_2[2], in_1[2], not_2_out);
  and and_7 (and_7_out, not_2_out, in_1[1]);
  and and_8 (and_8_out, in_2[2], in_1[0]);
  and and_9 (and_9_out, in_2[1], in_1[3], in_2[1]);
  and and_10 (and_10_out, in_2[1], in_1[2], not_3_out);
  and and_11 (and_11_out, not_3_out, in_1[1]);
  and and_12 (and_12_out, in_2[1], in_1[0]);
  and and_13 (and_13_out, in_2[0], in_1[3], in_2[0]);
  and and_14 (and_14_out, in_2[0], in_1[2], not_4_out);
  and and_15 (and_15_out, not_4_out, in_1[1]);
  and and_16 (and_16_out, in_2[0], in_1[0]);
  nor nor_1 (nor_1_out, and_1_out, and_2_out);
  nor nor_2 (nor_2_out, and_3_out, and_4_out, in_3[3]);
  nor nor_3 (nor_3_out, and_5_out, and_6_out);
  nor nor_4 (nor_4_out, and_7_out, and_8_out, in_3[2]);
  nor nor_5 (nor_5_out, and_9_out, and_10_out);
  nor nor_6 (nor_6_out, and_11_out, and_12_out, in_3[1]);
  nor nor_7 (nor_7_out, and_13_out, and_14_out);
  nor nor_8 (nor_8_out, and_15_out, and_16_out, in_3[0]);
  xor xor_1 (xor_1_out, nor_1_out, nor_2_out);
  xor xor_2 (xor_2_out, nor_3_out, nor_4_out);
  xor xor_3 (xor_3_out, nor_5_out, nor_6_out);
  xor xor_4 (xor_4_out, nor_7_out, nor_8_out);
  not not_5 (not_5_out, M);
  and and_17 (and_17_out, nor_1_out, nor_4_out);
  and and_18 (and_18_out, nor_1_out, nor_3_out, nor_6_out);
  and and_19 (and_19_out, nor_1_out, nor_3_out, nor_5_out, nor_8_out);
  nand nand_1 (nand_1_out, nor_1_out, nor_3_out, nor_7_out, nor_5_out, Cn_prime);
  nand nand_2 (X, nor_1_out, nor_3_out, nor_5_out, nor_7_out);
  and and_20 (and_20_out, Cn_prime, nor_7_out, nor_5_out, nor_3_out, not_5_out);
  and and_21 (and_21_out, nor_5_out, nor_3_out, nor_8_out, not_5_out);
  and and_22 (and_22_out, nor_3_out, nor_6_out, not_5_out);
  and and_23 (and_23_out, nor_4_out, not_5_out);
  and and_24 (and_24_out, Cn_prime, nor_7_out, nor_5_out, not_5_out);
  and and_25 (and_25_out, nor_5_out, nor_8_out, not_5_out);
  and and_26 (and_26_out, nor_6_out, not_5_out);
  and and_27 (and_27_out, Cn_prime, nor_7_out, not_5_out);
  and and_28 (and_28_out, nor_8_out, not_5_out);
  nand nand_3 (nand_3_out, Cn_prime, not_5_out);
  nor nor_9 (Y, nor_2_out, and_17_out, and_18_out, and_19_out);
  nor nor_10 (nor_10_out, and_20_out, and_21_out, and_22_out, and_23_out);
  nor nor_11 (nor_11_out, and_24_out, and_25_out, and_26_out);
  nor nor_12 (nor_12_out, and_27_out, and_28_out);
  not not_6 (not_6_out, Y);
  or or_1 (C_n_4_prime, not_6_out, not_7_out);
  not not_7 (not_7_out, nand_1_out);
  xor xor_5 (out_9[3], xor_1_out, nor_10_out);
  xor xor_6 (out_9[2], xor_2_out, nor_11_out);
  xor xor_7 (out_9[1], xor_3_out, nor_12_out);
  xor xor_8 (out_9[0], xor_4_out, nand_3_out);
  and and_29 (A_B, out_9[3], out_9[2], out_9[1], out_9[0]);

  // Other names for the same wires on the sheet: B0 = in_2[0]; B1 = in_2[1]; B2 = in_2[2]; B3 = in_2[3]; A0 = in_3[0];
  //   A1 = in_3[1]; A2 = in_3[2]; A3 = in_3[3]
endmodule
